# Fritzing sketch lane_follow_bot_wiring_diagram (saved by Fritzing 0.9.10b)
perfboards: 2
breadboards: 1

parts:
  M1 = Nucleo 144 MB1137
  Part1 = Bluetooth HC-05 Macho
  L298N1 = L298N DC motor driver
  M2 = gear-motor
  VCC2 = 4 x AAA Battery Mount
  M3 = gear-motor

nets:
  N1: M1.PC12, M1.SDMMC_CK/PC12, L298N1.IN1
  N2: M1.PD2, M1.SDMMC_CMD/PD2, L298N1.IN2
  +5V: M1.+5V, Part1.VCC
  N3: M1.PD5, M1.USART_B_TX/PD5, Part1.RXD
  N4: M1.PG2, L298N1.IN3
  N5: M1.PG3, L298N1.IN4
  GND: M1.GND, Part1.GND
  N6: M1.IOREF, M1.SDMMC_D1/PC9
  N7: M1.A0/PA3, M1.PA3, Part1.TXD
  N8: M1.PA7, M1.PE4
  N9: M1.I2C_B_SMBA/PF2, M1.PE5
  N10: M1.PB2, L298N1.ENA, L298N1.ENB
  N11: L298N1.OUT1, M3.pin_1
  N12: L298N1.OUT2, M3.pin_2
  N13: L298N1.OUT3, M2.pin_1
  N14: L298N1.OUT4, M2.pin_2
  N15: L298N1.12V, VCC2.+
  N16: L298N1.GND, VCC2.-

notes:
  D0
  VSYNC
  D4
  D2
  XCLK
  SIOD
  HREF
  PCLK
  GND
  D1
  OV7670 Camera Module
  PWDN
  D5
  RESET
  SIOC
  D3
  + VCC
  D7
  D6
  L298N H-Bridge
  DC Motor
  Bluetooth Module
  STM32F446ZE

custom parts:
  Nucleo 144 MB1137: The STM32 Nucleo-144 boards based on the MB1137 reference board (NUCLEO-F207ZG, NUCLEO-F303ZE, NUCLEO-F412ZG, NUCLEO-F413ZH, NUCLEO-F429ZI, NUCLEO-F439ZI, NUCLEO-F446ZE, NUCLEO-F722ZE, NUCLEO-F746ZG, NUCLEO-F756ZG, NUCLEO-F767ZI and NUCLEO-H743ZI) provide an affordable and flexible way for users to try out new concepts and build prototypes with STM32 microcontrollers.
  L298N DC motor driver: 2x DC motor driver with 78M05 positive voltage regulator (7..35 V) L298N: max 46 V, 2 A Set 5 V Enable jumper to enable 5 V regultor (needed for the L298N) and +5 V output at screw terminal or supply external +5 V at screw terminal Set ENA and/or ENB to +5 V to enable motor permanently or supply ENA and/or ENB with PWM signal IN1 and IN2 set rotation directory for motor A (OUT1/OUT2) IN2 and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
